# Fritzing sketch bethuneFinalProject (saved by Fritzing 0.9.1b)
breadboards: 1

parts:
  Part1 = Arduino Uno (Rev3)
  BAT1 = BC9VPC [package=bc9vpc]
  J1 = Basic Servo
  J2 = Basic Servo
  LED1 = LED - 5mm [color="Red (633nm)" package="5 mm [THT]"]
  LED2 = LED - 5mm [color="Red (633nm)" package="5 mm [THT]"]
  R1 = Resistor [tolerance=±5% resistance=220 package=THT]
  R2 = Resistor [tolerance=±5% resistance=220 package=THT]
  J3 = Piezo Speaker

nets:
  N1: Part1.D8, J3.pin1
  N2: Part1.D9_PWM, J2.pulse
  N3: Part1.D10_PWM/SS, J1.pulse
  N4: Part1.D12/MISO, LED2.cathode
  N5: Part1.D13/SCK, LED1.cathode
  GND: Part1.GND, BAT1.V-, J2.gnd, J3.pin2
  VCC: BAT1.V+, J1.vcc, J2.vcc, R1.Pin_1, R2.Pin_1
  N6: LED1.anode, R1.Pin_0
  N7: LED2.anode, R2.Pin_0
